// Logisim project PacMo.circ as structural Verilog: 1 circuit, main circuit main
module main (
  input  [1:0] ReadReg1,
  input  [1:0] WriteReg,
  input  [1:0] ReadReg2,
  input  [1:0] Opcode,
  output [15:0] RegData1,
  output [15:0] RegData2
);

  wire and_1_out, and_2_out, and_3_out, and_4_out, Clock1_out, comparator_1_eq, decoder_1_out0,
       decoder_1_out1, decoder_1_out2, decoder_1_out3, decoder_2_out0, decoder_2_out1, decoder_2_out2,
       decoder_2_out3, or_1_out;
  wire [1:0] ram_1_dout_2;
  wire [7:0] adder_1_out, PC_q, ram_1_dout_3;
  wire [15:0] adder_2_out, bit_extender_1_out, multiplexer_1_out, multiplexer_2_out, multiplexer_3_out,
       multiplexer_4_out, ram_1_dout, ram_2_dout, subtractor_1_out, X0_q, X1_q, X2_q, X3_q;

  RAM #(.dataWidth(16)) ram_1 (
    .addr(PC_q), .we(1'b0), .oe(1'b1), .clk(Clock1_out),
    .dout({ram_1_dout[15:14], ram_1_dout_3, ram_1_dout_2, ram_1_dout[3:0]}));  // open: din
  Clock Clock1 (.out(Clock1_out));
  Register PC (.D(adder_1_out), .clk(Clock1_out), .Q(PC_q));  // open: en, clr
  Adder adder_1 (.a(PC_q), .b(8'h1), .out(adder_1_out));  // open: cin, cout
  Decoder #(.enable("false"), .select(2)) decoder_1 (
    .out0(decoder_1_out0), .out1(decoder_1_out1), .out2(decoder_1_out2), .out3(decoder_1_out3),
    .sel(ram_1_dout[15:14]));
  Decoder #(.enable("false"), .select(2)) decoder_2 (
    .out0(decoder_2_out0), .out1(decoder_2_out1), .out2(decoder_2_out2), .out3(decoder_2_out3),
    .sel(ram_1_dout[1:0]));
  or or_1 (or_1_out, decoder_1_out0, decoder_1_out1, decoder_1_out2);
  Register #(.width(16)) X0 (.D(ram_2_dout), .en(and_1_out), .clk(Clock1_out), .Q(X0_q));  // open: clr
  and and_1 (and_1_out, or_1_out, decoder_2_out0);
  Register #(.width(16)) X1 (.D(ram_2_dout), .en(and_2_out), .clk(Clock1_out), .Q(X1_q));  // open: clr
  and and_2 (and_2_out, or_1_out, decoder_2_out1);
  Register #(.width(16)) X2 (.D(ram_2_dout), .en(and_3_out), .clk(Clock1_out), .Q(X2_q));  // open: clr
  and and_3 (and_3_out, or_1_out, decoder_2_out2);
  Register #(.width(16)) X3 (.D(ram_2_dout), .en(and_4_out), .clk(Clock1_out), .Q(X3_q));  // open: clr
  and and_4 (and_4_out, or_1_out, decoder_2_out3);
  Multiplexer #(.select(2), .width(16)) multiplexer_1 (
    .in0(X0_q), .in1(X1_q), .in2(X2_q), .in3(X3_q), .out(multiplexer_1_out), .sel(ram_1_dout[3:2]));
  Multiplexer #(.select(2), .width(16)) multiplexer_2 (
    .in0(X0_q), .in1(X1_q), .in2(X2_q), .in3(X3_q), .out(multiplexer_2_out), .sel(ram_1_dout_2));
  assign bit_extender_1_out = {{6{ram_1_dout_3[7]}}, {ram_1_dout_3, ram_1_dout_2}};  // Bit_Extender bit_extender_1
  Comparator comparator_1 (.a(8'hf0), .b(ram_1_dout_3), .eq(comparator_1_eq));  // open: gt, lt
  Multiplexer #(.width(16)) multiplexer_3 (
    .in0(bit_extender_1_out), .in1(multiplexer_2_out), .out(multiplexer_3_out), .sel(comparator_1_eq));
  Adder #(.width(16)) adder_2 (.a(multiplexer_1_out), .b(multiplexer_3_out), .out(adder_2_out));  // open: cin, cout
  Subtractor #(.width(16)) subtractor_1 (
    .a(multiplexer_1_out), .b(multiplexer_3_out), .out(subtractor_1_out));  // open: bin, bout
  Multiplexer #(.width(16)) multiplexer_4 (
    .in0(adder_2_out), .in1(subtractor_1_out), .out(multiplexer_4_out), .sel(decoder_1_out1));
  RAM #(.dataWidth(16)) ram_2 (
    .addr(PC_q), .we(decoder_1_out3), .oe(decoder_1_out2), .clk(Clock1_out), .din(multiplexer_4_out),
    .dout(ram_2_dout));
  Multiplexer #(.width(16)) multiplexer_5 (.sel(decoder_1_out2));  // open: in0, in1, out

  // Notes on the sheet:
  //   0050
  //   ADD X0, X1,X2
  //   Jake Paccione & Matthew Mohamed | Lab 8
  //   Opcode
  //   OpCode Add-00, Sub-01, LDR-10,STR-11
  //   Write Port
  //   MemRead
  //   MemWrite
  //   MemToReg
  //   RegWrite
  //   ReadReg1
  //   ReadReg2
  //   Read Port 1
  //   Read Port 2
endmodule
